# Fritzing sketch waterfall sketch (saved by Fritzing 0.9.3b)
breadboards: 1

parts:
  Part1 = Arduino Mega 2560 (Rev3)
  C1 = Electrolytic Capacitor [capacitance=1µF package="100 mil [THT, electrolytic]"]
  Strip_2 = Camdenboss CTB0158-4 [part_number=CTB0158-4 package=THT]
  Strip_0 = Camdenboss CTB0158-4 [part_number=CTB0158-4 package=THT]
  Strip_1 = Camdenboss CTB0158-4 [part_number=CTB0158-4 package=THT]
  Strip_4 = Camdenboss CTB0158-4 [part_number=CTB0158-4 package=THT]
  Strip_3 = Camdenboss CTB0158-4 [part_number=CTB0158-4 package=THT]

nets:
  5V: Part1.GND, C1.-, Strip_0.pin4
  N1: Part1.VIN, C1.+
  N2: Part1.D22, Strip_0.pin2
  N3: Part1.D23, Strip_0.pin3
  N4: Part1.D24, Strip_1.pin2
  N5: Part1.D25, Strip_1.pin3
  N6: Part1.D26, Strip_2.pin2
  N7: Part1.D27, Strip_2.pin3
  N8: Part1.D28, Strip_3.pin2
  N9: Part1.D29, Strip_3.pin3
  N10: Part1.D30, Strip_4.pin2
  N11: Part1.D31, Strip_4.pin3
  GND: Strip_0.pin1

notes:
  Brightness Pin (deprecated)
  Day - High
  Night - Low
  SCL is Brightness Pin
  Day - High
  Night - Low
  RX
  TX

// code stored in the sketch: waterfall.ino
#include <LocoNet.h>
#include <avr/power.h>
#include "Animation.cpp"


CRGB strip[STRIP_AMOUNT][STRIP_LENGTH];     // declares array of LED strips
bool not_visible;
uint8_t dim_current;
uint8_t dim_target;
uint8_t animation_selector;

lnMsg *LnPacket;
LocoNetThrottleClass Throttle;


/* 
 * Animationa declaration and related colours go here.
 * And yes, throughout this code I chose to use the Canadian spelling of colour. Sorry.
 * 
 */

// HSV values: H: Hue, S: Saturation (whiteness), V: Value (brighness)

Waterfall *waterfall;

const CHSV WATER(70, 180, 32);

const CHSV HIGHLIGHT(70, 90, 48);
const CHSV HIGHLIGHT_RATE(0, 15, 2);

const CHSV SHIMMER(20, 180, 32);
const CHSV SHIMMER_RATE(4, 0, 0);


OHML *ohml;

const CHSV ORANGE(150, 255, 255);
const CHSV WHITE(150, 64, 32);


/* 
 * HELPER METHODS
 * Do not use or edit.
 * ...or don't even worry about them.
 *
 */


// method controlling brightness for day / night modes based off of pin input
void dim_on_pin() {
  if (digitalRead(DAY_PIN) == HIGH && dim_current != 0) {
    dim_current = (dim_current <= DIM_RATE) ? 0 : dim_current - DIM_RATE;
  } else if (digitalRead(DAY_PIN) == LOW && dim_current != DIM_PERCENT) {
    dim_current = (DIM_PERCENT - dim_current <= DIM_RATE) ? DIM_PERCENT : dim_current + DIM_RATE;
  }
  
  for (int strip_num = 0; dim_current != 0 && strip_num < STRIP_AMOUNT; ++strip_num) {
    strip[strip_num][START].fadeLightBy(dim_current);
  }
}

// method controlling brightness for day / night modes based odd of class variable controlled by LocoNet
void dim_with_fading() {
  if (dim_current > dim_target) {
    dim_current = (dim_current - dim_target <= DIM_RATE) ? dim_target : dim_current - DIM_RATE;
  } else if (dim_current < dim_target){
    dim_current = (dim_target - dim_current <= DIM_RATE) ? dim_target : dim_current + DIM_RATE;
  }

  if(dim_current != 0) {
    for (int strip_num = 0; strip_num < STRIP_AMOUNT; ++strip_num) {
      strip[strip_num][START].fadeLightBy(dim_current);
    }
  }
}

// simplified version of method above
void dim_quick() {
  if(dim_target != 0) {
    for (int strip_num = 0; strip_num < STRIP_AMOUNT; ++strip_num) {
      strip[strip_num][START].fadeLightBy(dim_target);
    }
  }
}

// shifts every light down to create illusion of flow
void flow(int wait_time) {

  // if the direction in the software is backwards, turn off the flow; the animations will continue running but they will not be visible
  if (not_visible) {
    for (int strip_num = 0; strip_num < STRIP_AMOUNT; ++strip_num) {
      strip[strip_num][START] = 0;
    }
  }
  
  dim_quick();
  FastLED.show();
  
  for (int strip_num = 0; strip_num < STRIP_AMOUNT; ++strip_num) {
    for (int pos = STRIP_LENGTH - 1; pos > START; --pos) {
      strip[strip_num][pos] = strip[strip_num][pos - 1];
    }
  }
  
  delay(wait_time);
}


/*
 * Scary LocoNet stuff.
 * 
 */


// user-defined callback functions
void notifyThrottleAddress(uint8_t UserData, TH_STATE State, uint16_t Address, uint8_t Slot)    {Serial.print("Address: ");     Serial.println(Address);}
void notifyThrottleSlotStatus(uint8_t UserData, uint8_t Status)                                 {Serial.print("Slot Status: "); Serial.println(Status);}
void notifyThrottleError(uint8_t UserData, TH_ERROR Error)                                      {Serial.print("Error: ");       Serial.println(Throttle.getErrorStr(Error));}
void notifyThrottleState(uint8_t UserData, TH_STATE PrevState, TH_STATE State)                  {Serial.print("State: ");       Serial.println(Throttle.getStateStr(State));}
void notifyThrottleSpeed(uint8_t UserData, TH_STATE State, uint8_t Speed)                       {Serial.print("Speed: ");       Serial.println(Speed); dim_target = 2 * (127 - Speed);}
void notifyThrottleDirection(uint8_t UserData, TH_STATE State, uint8_t Direction)               {Serial.print("Direction: ");   Serial.println(not_visible = Direction);}
void notifyThrottleFunction(uint8_t UserData, uint8_t Function, uint8_t Value)                  {Serial.print("Function: ");    Serial.println(Function);
                                                                                                 animation_selector = (Function < NUM_ANIMATIONS) ? Function : 0;}


// used for printing and processing LocoNet packets
void lnUpdate() {
  LnPacket = LocoNet.receive() ;
  if (LnPacket) {
    
    // First print out the packet in HEX
    Serial.print("RX: ");
    uint8_t msgLen = getLnMsgSize(LnPacket);
    for (uint8_t x = 0; x < msgLen; x++)
    {
      uint8_t val = LnPacket->data[x];
      // Print a leading 0 if less than 16 to make 2 HEX digits
      if (val < 16)
        Serial.print('0');

      Serial.print(val, HEX);
      Serial.print(' ');
    }

    // If this packet was not a Switch or Sensor Message then print a new line, and process it as a Throttle Message
    if (!LocoNet.processSwitchSensorMessage(LnPacket)) {
      Serial.println();
      Throttle.processMessage(LnPacket);
    }
  }
}

/*
 * RUNNABLE FUNCTIONS
 * Feel free to use, but do not edit.
 */

// runs an animation with a given delay; default is no delay
void animation_runner(Animation *a1, int wait_time = 0) {
  CHSV *row = a1->getNext(animation_selector);
  while(row != NULL) {
    for (int strip_num = 0; strip_num < STRIP_AMOUNT; ++strip_num) {
      strip[strip_num][START] = row[strip_num];
    }
    flow(wait_time);
    row = a1->getNext(animation_selector);

    lnUpdate();
  }
}


/*
 * DEFAULT ARDUINO METHODS
 * Feel free to edit at will.
 * 
 */


// initial setup function
void setup() {

  // initialization of hardware and background variables (try not to edit this)

  Serial.begin(9600);

  pinMode(DAY_PIN, INPUT);
  
  if (0 < STRIP_AMOUNT) FastLED.addLeds<APA102, STRIP0_DATA_PIN, STRIP0_CLOCK_PIN>(strip[0], STRIP_LENGTH);
  if (1 < STRIP_AMOUNT) FastLED.addLeds<APA102, STRIP1_DATA_PIN, STRIP1_CLOCK_PIN>(strip[1], STRIP_LENGTH);
  if (2 < STRIP_AMOUNT) FastLED.addLeds<APA102, STRIP2_DATA_PIN, STRIP2_CLOCK_PIN>(strip[2], STRIP_LENGTH);
  if (3 < STRIP_AMOUNT) FastLED.addLeds<APA102, STRIP3_DATA_PIN, STRIP3_CLOCK_PIN>(strip[3], STRIP_LENGTH);
  if (4 < STRIP_AMOUNT) FastLED.addLeds<APA102, STRIP4_DATA_PIN, STRIP4_CLOCK_PIN>(strip[4], STRIP_LENGTH);

  FastLED.show();   //display strips to clear previous run
  
  Serial.println("Initialized Strips");
  
  
  // initialize Animation objects here; see possible Animations and their constructors in Animation.cpp
  waterfall = new Waterfall(0, WATER, HIGHLIGHT, SHIMMER, HIGHLIGHT_RATE, SHIMMER_RATE, false, false, 3, 7);
  ohml = new OHML(1, ORANGE, WHITE);
  
  Serial.println("Initialized Animations"); 
   

  // setup LocoNet and Throttle
  LocoNet.init(TX_PIN);
  Throttle.init(0, 0, LOCO_ADDRESS);

  // attempt to initialize onto existing address
  Serial.println("\tStealing Address");
  Throttle.stealAddress(LOCO_ADDRESS);
  lnUpdate();     // repeated to process possible errors
  lnUpdate();     // do not remove duplicate line

  // if address does not exist, create one
  if (Throttle.getState() == TH_ST_FREE) {
    Serial.println("\nSetting Address");
    Throttle.setAddress(LOCO_ADDRESS);
  }
  lnUpdate();

  Serial.println("Established connection with LocoNet");


  // initialize variables that have been written over with the loconet update calls
  dim_current = 0;
  animation_selector = 0;

  Serial.println("Initialized Starting Configuration");
  
  
  Serial.println("\nExiting Setup\n");
}

// continuous loop
void loop() {
  animation_runner(waterfall);
  animation_runner(ohml);
}
